// Logisim project batalhaNaval.circ as structural Verilog: 8 circuits, main circuit main
module main (
  input  in_1,
  input  in_2,
  input  in_3,
  input  in_4,
  input  in_5,
  input  in_6,
  input  in_7,
  input  in_8,
  output AcertouNavio
);

  wire decodificador_1_saidas1, decodificador_1_saidas2, decodificador_1_saidas3, decodificador_1_saidas4;

  Decodificador decodificador_1 (
    .A(in_1), .B(in_2), .C(in_3), .D(in_4), .SaidaS1(decodificador_1_saidas1),
    .SaidaS2(decodificador_1_saidas2), .SaidaS3(decodificador_1_saidas3), .SaidaS4(decodificador_1_saidas4));
  Comparador comparador_1 (
    .Bit0DoNavio(in_5), .Bit0DoTIro(decodificador_1_saidas1), .Bit1DoNavio(in_6),
    .Bit1DoTIro(decodificador_1_saidas2), .Bit2DoNavio(in_7), .Bit2DoTIro(decodificador_1_saidas3),
    .Bit3DoNavio(in_8), .Bit3DoTIro(decodificador_1_saidas4), .out_9(AcertouNavio));
endmodule

module S1 (
  input  A,
  input  B,
  input  C,
  input  D,
  output out_5
);

  wire and_1_out, and_2_out, and_3_out, nor_1_out, not_1_out, not_2_out, not_3_out;

  not not_1 (not_1_out, A);
  not not_2 (not_2_out, B);
  not not_3 (not_3_out, D);
  nor nor_1 (nor_1_out, A, B);
  and and_1 (and_1_out, not_1_out, D);
  and and_2 (and_2_out, not_2_out, C, not_3_out);
  and and_3 (and_3_out, B, C, D);
  or or_1 (out_5, nor_1_out, and_1_out, and_2_out, and_3_out);
endmodule

module S2 (
  input  A,
  input  B,
  input  C,
  input  D,
  output out_5
);

  wire and_1_out, and_2_out, and_3_out, not_1_out, not_2_out, not_3_out, not_4_out;

  not not_1 (not_1_out, A);
  not not_2 (not_2_out, B);
  not not_3 (not_3_out, C);
  not not_4 (not_4_out, D);
  and and_1 (and_1_out, A, not_2_out, C);
  and and_2 (and_2_out, not_2_out, not_3_out, D);
  and and_3 (and_3_out, not_1_out, not_4_out);
  or or_1 (out_5, and_1_out, and_2_out, and_3_out);
endmodule

module S3 (
  input  A,
  input  B,
  input  C,
  input  D,
  output out_5
);

  wire and_1_out, and_2_out, and_3_out, nor_1_out, nor_2_out, not_1_out, not_2_out, not_3_out;

  not not_1 (not_1_out, A);
  not not_2 (not_2_out, B);
  not not_3 (not_3_out, C);
  and and_1 (and_1_out, not_1_out, B, C);
  nor nor_1 (nor_1_out, B, C, D);
  and and_2 (and_2_out, not_2_out, C, D);
  and and_3 (and_3_out, A, B, not_3_out, D);
  nor nor_2 (nor_2_out, A, B, C);
  or or_1 (out_5, and_1_out, nor_1_out, and_2_out, and_3_out, nor_2_out);
endmodule

module S4 (
  input  A,
  input  B,
  input  C,
  input  D,
  output out_5
);

  wire and_1_out, and_2_out, and_3_out, nor_1_out, nor_2_out, not_1_out;

  nor nor_1 (nor_1_out, A, B);
  not not_1 (not_1_out, D);
  and and_1 (and_1_out, nor_1_out, C);
  and and_2 (and_2_out, A, B, D);
  and and_3 (and_3_out, B, C, not_1_out);
  nor nor_2 (nor_2_out, D, A);
  or or_1 (out_5, nor_2_out, and_1_out, and_2_out, and_3_out);
endmodule

module ComparadorDeBit (
  input  BitDoNavio,
  input  BitDoTiro,
  output out_3
);

  wire xor_1_out;

  xor xor_1 (xor_1_out, BitDoNavio, BitDoTiro);
  not not_1 (out_3, xor_1_out);
endmodule

module Decodificador (
  input  A,
  input  B,
  input  C,
  input  D,
  output SaidaS1,
  output SaidaS2,
  output SaidaS3,
  output SaidaS4
);

  S1 s1_1 (.A(A), .B(B), .C(C), .D(D), .out_5(SaidaS1));
  S2 s2_1 (.A(A), .B(B), .C(C), .D(D), .out_5(SaidaS2));
  S3 s3_1 (.A(A), .B(B), .C(C), .D(D), .out_5(SaidaS3));
  S4 s4_1 (.A(A), .B(B), .C(C), .D(D), .out_5(SaidaS4));
endmodule

module Comparador (
  input  Bit0DoNavio,
  input  Bit0DoTIro,
  input  Bit1DoNavio,
  input  Bit1DoTIro,
  input  Bit2DoNavio,
  input  Bit2DoTIro,
  input  Bit3DoNavio,
  input  Bit3DoTIro,
  output out_9
);

  wire comparadordebit_1_out_3, comparadordebit_2_out_3, comparadordebit_3_out_3, comparadordebit_4_out_3;

  ComparadorDeBit comparadordebit_1 (.BitDoNavio(Bit0DoNavio), .BitDoTiro(Bit0DoTIro), .out_3(comparadordebit_1_out_3));
  ComparadorDeBit comparadordebit_2 (.BitDoNavio(Bit1DoNavio), .BitDoTiro(Bit1DoTIro), .out_3(comparadordebit_2_out_3));
  ComparadorDeBit comparadordebit_3 (.BitDoNavio(Bit2DoNavio), .BitDoTiro(Bit2DoTIro), .out_3(comparadordebit_3_out_3));
  ComparadorDeBit comparadordebit_4 (.BitDoNavio(Bit3DoNavio), .BitDoTiro(Bit3DoTIro), .out_3(comparadordebit_4_out_3));
  and and_1 (out_9, comparadordebit_1_out_3, comparadordebit_2_out_3, comparadordebit_3_out_3, comparadordebit_4_out_3);
endmodule
